# Fritzing sketch turing_alarm (saved by Fritzing 0.6.3b)
breadboards: 2

parts:
  Arduino1 = Arduino
  IC2 = DS1307 [package=THT]
  XTAL1 = Crystal [frequency=20MHz package=THT]
  J1 = Piezo Speaker
  S1 = Pushbutton [package="[THT]"]
  R1 = Resistor [tolerance=±5% resistance=220 package=THT]
  S2 = Pushbutton [package="[THT]"]
  R2 = Resistor [tolerance=±5% resistance=220 package=THT]
  S3 = Pushbutton [package="[THT]"]
  R3 = Resistor [tolerance=±5% resistance=220 package=THT]
  S4 = Pushbutton [package="[THT]"]
  R4 = Resistor [tolerance=±5% resistance=220 package=THT]
  S5 = Pushbutton [package="[THT]"]
  R5 = Resistor [tolerance=±5% resistance=220 package=THT]
  LCD1 = LCD screen
  R6 = Resistor [tolerance=±5% resistance=10k package=THT]
  R7 = Resistor [tolerance=±5% resistance=100 package=THT]

nets:
  N1: Arduino1.GND, IC2.0V, J1.pin1, S1.Pin_1, S1.Pin_2, R1.Pin_1, R2.Pin_1, S3.Pin_1, S3.Pin_2, R3.Pin_1, S4.Pin_1, S4.Pin_2, R4.Pin_1, S5.Pin_1, S5.Pin_2, R5.Pin_1
  N2: Arduino1.D9, J1.pin2
  N3: Arduino1.D8, S5.Pin_3, S5.Pin_4, R5.Pin_0
  N4: Arduino1.D5, S4.Pin_3, S4.Pin_4, R4.Pin_0
  N5: Arduino1.D4, S3.Pin_3, S3.Pin_4, R3.Pin_0
  N6: Arduino1.D3, S2.Pin_3, S2.Pin_4, R2.Pin_0
  N7: Arduino1.D2, S1.Pin_3, S1.Pin_4, R1.Pin_0
  N8: Arduino1.D1TX, LCD1.VSS
  N9: Arduino1.+5V, IC2.+V, R6.Pin_1, R7.Pin_1
  N10: Arduino1.A4, IC2.SDA_-_I2C_Data
  N11: Arduino1.A5, IC2.SCL_-_I2C_Clock, R6.Pin_0, R7.Pin_0
  N12: IC2.X1_-_Crystal, XTAL1.pin_0
  N13: IC2.X2_-_Crystal, XTAL1.pin_1
  N14: S2.Pin_1, S2.Pin_2
